# Fritzing sketch Skematik Robot Line Follower (saved by Fritzing 0.9.3b)
breadboards: 1

parts:
  Part1 = Arduino Nano (Rev3.0)
  Part2 = NRF24L01+ Breakout Board
  TCRT1 = TCRT5000 sensor module [part_number=151608]
  M4 = DC Motor  # not connected
  M5 = DC Motor  # not connected
  VCC2 = 4 x AAA Battery Mount  # not connected
  TCRT2 = TCRT5000 sensor module [part_number=151608]
  TCRT3 = TCRT5000 sensor module [part_number=151608]
  TCRT4 = TCRT5000 sensor module [part_number=151608]
  J1 = Basic Servo
  J3 = Basic Servo
  L298N2 = L298N DC motor driver

nets:
  GND: Part1.GND, Part2.GND, TCRT3.T-, J1.gnd
  N1: Part1.D2, TCRT1.D-
  N2: Part1.D3, TCRT2.D-
  N3: Part1.D5, J1.pulse
  N4: Part1.D6, J3.pulse
  N5: Part1.D7, TCRT3.D-
  N6: Part1.D8, TCRT4.D-
  N7: Part1.D9, L298N2.ENA
  N8: Part1.D10, L298N2.ENB
  N9: Part1.D11/MOSI, Part2.MOSI
  N10: Part1.D12/MISO, Part2.MISO
  VCC: Part1.5V, Part2.VCC, TCRT1.T+, J1.vcc
  N11: Part1.A5, L298N2.IN4
  N12: Part1.A4, L298N2.IN3
  N13: Part1.A3, L298N2.IN2
  N14: Part1.A2, L298N2.IN1
  N15: Part1.A1, Part2.CS
  N16: Part1.A0, Part2.CE
  N17: Part1.D13/SCK, Part2.SCK

notes:
  Max Voltage 12V
  IR Sensor
  Arduino Nano
  Motor Servo
  Motor 12 V DC
  nRF24l01
  Motor Driver L298N

custom parts:
  TCRT5000 sensor module: breakout board with TCRT5000
  L298N DC motor driver: 2x DC motor driver with 78M05 positive voltage regulator (7..35 V) L298N: max 46 V, 2 A Set 5 V Enable jumper to enable 5 V regultor (needed for the L298N) and +5 V output at screw terminal or supply external +5 V at screw terminal Set ENA and/or ENB to +5 V to enable motor permanently or supply ENA and/or ENB with PWM signal IN1 and IN2 set rotation directory for motor A (OUT1/OUT2) IN2 and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
